# Fritzing sketch WiiBravo (saved by Fritzing 0.9.3b)
breadboards: 1

parts:
  パーツ1 = Arduino Pro Mini v13
  J1 = Camdenboss CTB0158-9 [part_number=CTB0158-9 package=THT]
  R4 = Resistor [tolerance=±5% resistance=560 package=THT]
  R2 = Resistor [tolerance=±5% resistance=1k package=THT]
  LED3 = LED - 3mm [color="Blue (430nm)" package="3 mm [THT]"]
  LED1 = LED - 3mm [color="Red (633nm)" package="3 mm [THT]"]
  R1 = Resistor [tolerance=±5% resistance=1k package=THT]
  LED2 = LED - 3mm [color="Yellow (595nm)" package="3 mm [THT]"]
  R3 = Resistor [tolerance=±5% resistance=1k package=THT]

nets:
  N1: パーツ1.GND, J1.pin4, LED3.cathode, LED1.cathode, LED2.cathode
  N2: パーツ1.VCC, J1.pin5, R4.Pin_0
  N3: パーツ1.D8, R3.Pin_1
  N4: パーツ1.D7, R2.Pin_1
  N5: パーツ1.D6_PWM, R1.Pin_1
  N6: パーツ1.D5_PWM, J1.pin7
  N7: パーツ1.D4, J1.pin6
  N8: パーツ1.D3_PWM, J1.pin2
  N9: パーツ1.D2, J1.pin1, R4.Pin_1
  N10: R2.Pin_0, LED2.anode
  N11: LED3.anode, R3.Pin_0
  N12: LED1.anode, R1.Pin_0

notes:
  PlayStation Arduino
  1. Data 2
  2. Command 3
  3. NC
  4. Gnd GND
  5. 3.3V VCC
  6. Attention 4
  7. Clock 5
  8. NC
  9. NC
  Wiimote Arduino
  1. VCC (Red) VCC
  2. SCL (Yellow) A5
  3. NC
  4. NC
  5. SDA (Green) A4
  6. GND (White) GND
  D6 - R1 - LED1 (Red)
  D7 - R2 - LED2 (Yellow)
  D8 - R3 - LED3 (Blue)
